# Fritzing sketch Øving 4 Zumo (saved by Fritzing 0.9.3b)
breadboards: 1

parts:
  Part1 = Arduino Uno (Rev3)
  HC-SR04_Sensor_1 = HC-SR04 Ultrasonic Distance Sensor
  HC-SR04_Sensor_2 = HC-SR04 Ultrasonic Distance Sensor
  HC-SR04_Sensor_3 = HC-SR04 Ultrasonic Distance Sensor

nets:
  N1: Part1.D13/SCK, HC-SR04_Sensor_1.TRIG
  N2: Part1.D0/RX, HC-SR04_Sensor_3.ECHO
  N3: Part1.D1/TX, HC-SR04_Sensor_2.TRIG
  N4: Part1.D2, HC-SR04_Sensor_2.ECHO
  N5: Part1.D3_PWM, HC-SR04_Sensor_1.ECHO
  N6: Part1.D6_PWM, HC-SR04_Sensor_3.TRIG
  VCC: Part1.5V, HC-SR04_Sensor_1.VCC, HC-SR04_Sensor_2.VCC, HC-SR04_Sensor_3.VCC
  GND: Part1.GND, HC-SR04_Sensor_1.GND, HC-SR04_Sensor_2.GND, HC-SR04_Sensor_3.GND
